// Logisim project 8bit immedate Team 4 (1).circ as structural Verilog: 6 circuits, main circuit main
module main (
  input  [7:0] Pc_In,
  output [15:0] out_2,
  output ODD_party,
  output Even_Party,
  output Zero,
  output Sign,
  output Half_Carry
);

  wire clock_1_out, control_unit_1_alu, control_unit_1_ir, control_unit_1_mem_read,
       control_unit_1_operand_fetch, control_unit_1_pc_enable, control_unit_1_r_w_prime, not_1_out, reset;
  wire [7:0] MAR_q, pc_1_pc_out, RA, RB, Reg, Res;
  wire [15:0] MBR_q, rom_1_data;
  wire [15:8] IR_q, register_2_q;

  Control_Unit control_unit_1 (
    .Clock(clock_1_out), .Reset(reset), .PC_enable(control_unit_1_pc_enable),
    .Mem_read(control_unit_1_mem_read), .IR(control_unit_1_ir), .Operand_fetch(control_unit_1_operand_fetch),
    .ALU(control_unit_1_alu), .R_W_prime(control_unit_1_r_w_prime));
  Clock clock_1 (.out(clock_1_out));
  Button button_1 (.out(reset));
  PC pc_1 (
    .PC_in(Pc_In), .PC_enable(control_unit_1_pc_enable), .Clock(clock_1_out), .Reset(reset),
    .PC_out(pc_1_pc_out));
  LED led_1 (.in(reset));
  Register MAR (.D(pc_1_pc_out), .en(control_unit_1_pc_enable), .Q(MAR_q), .clk(clock_1_out), .clr(reset));
  not not_1 (not_1_out, control_unit_1_r_w_prime);
  ROM #(.dataWidth(16)) rom_1 (.addr(MAR_q), .data(rom_1_data));  // open: sel
  Register register_1 (.D(Reg), .en(control_unit_1_operand_fetch), .Q(RA), .clk(clock_1_out), .clr(reset));
  Register #(.width(16)) MBR (.D(rom_1_data), .en(control_unit_1_mem_read), .Q(MBR_q), .clk(clock_1_out), .clr(reset));
  Register #(.width(16)) IR (.D(MBR_q), .en(control_unit_1_ir), .Q({IR_q, RB}), .clk(clock_1_out), .clr(reset));
  ALU alu_1 (.A(RA), .B(RB), .S2_S1_S0(IR_q[15:12]), .Y(out_2));
  Reg_Bank reg_bank_1 (
    .D7D6___________D0(Res), .clk(clock_1_out), .R_W_prime(not_1_out), .S3S2S1S0(IR_q[11:8]), .out_5(Reg));
  Register #(.width(16)) register_2 (
    .D(out_2), .en(control_unit_1_alu), .Q({register_2_q, Res}), .clk(clock_1_out), .clr(reset));
  Hex_Digit_Display hex_digit_display_1 (.value(RA[7:4]));  // open: dp
  Hex_Digit_Display hex_digit_display_2 (.value(RA[3:0]));  // open: dp
  Hex_Digit_Display hex_digit_display_3 (.value(RB[7:4]));  // open: dp
  Hex_Digit_Display hex_digit_display_4 (.value(RB[3:0]));  // open: dp
  Hex_Digit_Display hex_digit_display_5 (.value(out_2[15:12]));  // open: dp
  Hex_Digit_Display hex_digit_display_6 (.value(out_2[11:8]));  // open: dp
  Psw PSW (
    .INPUT(out_2), .OP_2(RA), .OP_1(RB), .ODD_PARITY(ODD_party), .EVEN_PARITY(Even_Party), .ZERO(Zero),
    .SIGN_BIT(Sign), .HALF_CARRY(Half_Carry));
  Hex_Digit_Display hex_digit_display_7 (.value(out_2[3:0]));  // open: dp
  Hex_Digit_Display hex_digit_display_8 (.value(out_2[7:4]));  // open: dp

  // Other names for the same wires on the sheet: RZ[15:0] = out_2

  // Notes on the sheet:
  //   CU
  //   CLOCK
  //   PC
  //   CODE MEMORY
  //   contents of rom_1 (hex, n*v repeats v):
  //   3010 5106 1321
  //   ALU
  //   Reg Bank
  //   A
  //   B
  //   Result
endmodule

module ALU (
  input  [7:0] A,
  input  [7:0] B,
  input  [3:0] S2_S1_S0,
  output [15:0] Y
);

  wire adder_2_cout, subtractor_1_bout;
  wire [2:0] bit_extender_2_out;
  wire [7:0] adder_1_out, adder_2_out, and_1_out, bit_extender_1_out, bit_extender_5_out, bit_extender_6_out,
       bit_extender_16_out, divider_1_out, divider_1_rem, multiplier_1_cout, multiplier_1_out, not_1_out,
       or_1_out, shifter_1_out, shifter_2_out, shifter_3_out, shifter_4_out, subtractor_1_out,
       subtractor_2_out;
  wire [15:0] bit_extender_3_out, bit_extender_4_out, bit_extender_7_out, bit_extender_8_out,
       bit_extender_9_out, bit_extender_10_out, bit_extender_11_out, bit_extender_12_out,
       bit_extender_13_out, bit_extender_14_out, bit_extender_15_out;

  assign bit_extender_1_out = {{7{1'b0}}, 1'b1};  // Bit_Extender bit_extender_1
  Bit_Extender #(.out_width(3)) bit_extender_2 (.in(B), .out(bit_extender_2_out));
  Subtractor subtractor_1 (.a(A), .b(B), .out(subtractor_1_out), .bout(subtractor_1_bout));  // open: bin
  Multiplier multiplier_1 (.a(A), .b(B), .out(multiplier_1_out), .cout(multiplier_1_cout));  // open: cin
  Divider divider_1 (.a(A), .b(B), .out(divider_1_out), .rem(divider_1_rem));  // open: upper
  Adder adder_1 (.a(A), .b(bit_extender_1_out), .out(adder_1_out));  // open: cin, cout
  Subtractor subtractor_2 (.a(A), .b(bit_extender_1_out), .out(subtractor_2_out));  // open: bin, bout
  assign and_1_out = A & B;  // AND_Gate and_1, 8 bits wide
  assign or_1_out = A | B;  // OR_Gate or_1, 8 bits wide
  assign not_1_out = ~A;  // NOT_Gate not_1, 8 bits wide
  Shifter #(.shift("lr")) shifter_1 (.in(A), .\dist (bit_extender_2_out), .out(shifter_1_out));
  Shifter shifter_2 (.in(A), .\dist (bit_extender_2_out), .out(shifter_2_out));
  Shifter #(.shift("rr")) shifter_3 (.in(A), .\dist (bit_extender_2_out), .out(shifter_3_out));
  Shifter #(.shift("rl")) shifter_4 (.in(A), .\dist (bit_extender_2_out), .out(shifter_4_out));
  assign bit_extender_3_out = {{8{1'b0}}, B};  // Bit_Extender bit_extender_3
  assign bit_extender_4_out = {{8{1'b0}}, A};  // Bit_Extender bit_extender_4
  Adder adder_2 (.a(A), .b(B), .out(adder_2_out), .cout(adder_2_cout));  // open: cin
  assign bit_extender_5_out = {{7{1'b0}}, adder_2_cout};  // Bit_Extender bit_extender_5
  assign bit_extender_6_out = {{7{1'b0}}, subtractor_1_bout};  // Bit_Extender bit_extender_6
  assign bit_extender_7_out = {{8{1'b0}}, adder_1_out};  // Bit_Extender bit_extender_7
  assign bit_extender_8_out = {{8{1'b0}}, subtractor_2_out};  // Bit_Extender bit_extender_8
  assign bit_extender_9_out = {{8{1'b0}}, and_1_out};  // Bit_Extender bit_extender_9
  assign bit_extender_10_out = {{8{1'b0}}, or_1_out};  // Bit_Extender bit_extender_10
  assign bit_extender_11_out = {{8{1'b0}}, not_1_out};  // Bit_Extender bit_extender_11
  assign bit_extender_12_out = {{8{1'b0}}, shifter_1_out};  // Bit_Extender bit_extender_12
  assign bit_extender_13_out = {{8{1'b0}}, shifter_2_out};  // Bit_Extender bit_extender_13
  assign bit_extender_14_out = {{8{1'b0}}, shifter_3_out};  // Bit_Extender bit_extender_14
  assign bit_extender_15_out = {{8{1'b0}}, shifter_4_out};  // Bit_Extender bit_extender_15
  Multiplexer #(.select(4), .width(16), .enable("false")) multiplexer_1 (
    .in0(bit_extender_3_out), .in1(bit_extender_4_out), .in2({bit_extender_5_out, adder_2_out}),
    .in3({bit_extender_6_out, subtractor_1_out}), .in4({multiplier_1_cout, multiplier_1_out}),
    .in5({divider_1_rem, divider_1_out}), .in6(bit_extender_7_out), .in7(bit_extender_8_out),
    .in8(bit_extender_9_out), .in9(bit_extender_10_out), .in10(bit_extender_11_out), .in11({A, B}),
    .in12(bit_extender_12_out), .in13(bit_extender_13_out), .in14(bit_extender_14_out),
    .in15(bit_extender_15_out), .out(Y), .sel(S2_S1_S0));
  Bit_Extender #(.in_width(16), .out_width(8)) bit_extender_16 (.in(Y), .out(bit_extender_16_out));
  Hex_Digit_Display hex_digit_display_1 (.value(bit_extender_16_out[7:4]));  // open: dp
  Hex_Digit_Display hex_digit_display_2 (.value(bit_extender_16_out[3:0]));  // open: dp

  // Notes on the sheet:
  //   Using Multiplexer Creating ALU and with 16 Operations
  //   Increment-----------------------------
  //   Decrement-----------------------
  //   MUL
  //   Div
  //   AND
  //   OR
  //   Shift Right
  //   ADD
  //   SUB
  //   NOT
  //   Exchange
  //   Shift Left
  //   Rotate Right
  //   Rotate Left
  //   Load
  //   Store
  //   0000 - LOAD
  //   0001 -STORE
  //   0010 - ADD
  //   0011 - SUB
  //   0100 - MUL
  //   0101 - DIV
  //   0110 -Increment
  //   1000 - AND
  //   1001 - OR
  //   1010 - NOT
  //   0111 -Decrement
  //   1011 - EXCHANGE
  //   1100  -Shift Right
  //   1101  -Shift Left
  //   1110   Rotate Right
  //   1111  -  Rotate Left
endmodule

module PC (
  input  [7:0] PC_in,
  input  PC_enable,
  input  Clock,
  input  Reset,
  output [7:0] PC_out
);

  wire [7:0] adder_1_out;

  Adder adder_1 (.a(PC_in), .b(PC_out), .out(adder_1_out));  // open: cin, cout
  Hex_Digit_Display hex_digit_display_1 (.value(PC_out[7:4]));  // open: dp
  Register register_1 (.D(adder_1_out), .en(PC_enable), .Q(PC_out), .clk(Clock), .clr(Reset));
  Hex_Digit_Display hex_digit_display_2 (.value(PC_out[3:0]));  // open: dp

  // Notes on the sheet:
  //   Program Counter
endmodule

module Control_Unit (
  input  Clock,
  input  Reset,
  output PC_enable,
  output Mem_read,
  output IR,
  output Operand_fetch,
  output ALU,
  output R_W_prime
);

  wire [2:0] counter_1_q;

  Counter #(.width(3), .max('h7)) counter_1 (.Q(counter_1_q), .clk(Clock), .clr(Reset));  // open: load, D, count, carry
  Decoder #(.select(3), .enable("false")) decoder_1 (
    .out0(PC_enable), .out1(Mem_read), .out2(IR), .out3(Operand_fetch), .out4(ALU), .out5(R_W_prime),
    .sel(counter_1_q));  // open: out6, out7

  // Notes on the sheet:
  //   CONTROL UNIT
endmodule

module Reg_Bank (
  input  [7:0] D7D6___________D0,
  input  clk,
  input  R_W_prime,
  input  [3:0] S3S2S1S0,
  output [7:0] out_5
);

  wire decoder_1_out0, decoder_1_out1, decoder_1_out2, decoder_1_out3, decoder_1_out4, decoder_1_out5,
       decoder_1_out6, decoder_1_out7, decoder_1_out8, decoder_1_out9, decoder_1_out10, decoder_1_out11,
       decoder_1_out12, decoder_1_out13, decoder_1_out14, decoder_1_out15, not_1_out;
  wire [7:0] register_1_q, register_2_q, register_3_q, register_4_q, register_5_q, register_6_q,
       register_7_q, register_8_q, register_9_q, register_10_q, register_11_q, register_12_q, register_13_q,
       register_14_q, register_15_q, register_16_q;

  not not_1 (not_1_out, R_W_prime);
  Hex_Digit_Display hex_digit_display_1 (.value(D7D6___________D0[7:4]));  // open: dp
  Decoder #(.select(4), .disabled(0)) decoder_1 (
    .out0(decoder_1_out0), .out1(decoder_1_out1), .out2(decoder_1_out2), .out3(decoder_1_out3),
    .out4(decoder_1_out4), .out5(decoder_1_out5), .out6(decoder_1_out6), .out7(decoder_1_out7),
    .out8(decoder_1_out8), .out9(decoder_1_out9), .out10(decoder_1_out10), .out11(decoder_1_out11),
    .out12(decoder_1_out12), .out13(decoder_1_out13), .out14(decoder_1_out14), .out15(decoder_1_out15),
    .sel(S3S2S1S0), .en(not_1_out));
  Hex_Digit_Display hex_digit_display_2 (.value(D7D6___________D0[3:0]));  // open: dp
  Register register_1 (.D(D7D6___________D0), .en(decoder_1_out0), .Q(register_1_q), .clk(clk));  // open: clr
  Register register_2 (.D(D7D6___________D0), .en(decoder_1_out1), .Q(register_2_q), .clk(clk));  // open: clr
  Register register_3 (.D(D7D6___________D0), .en(decoder_1_out2), .Q(register_3_q), .clk(clk));  // open: clr
  Register register_4 (.D(D7D6___________D0), .en(decoder_1_out3), .Q(register_4_q), .clk(clk));  // open: clr
  Register register_5 (.D(D7D6___________D0), .en(decoder_1_out4), .Q(register_5_q), .clk(clk));  // open: clr
  Register register_6 (.D(D7D6___________D0), .en(decoder_1_out5), .Q(register_6_q), .clk(clk));  // open: clr
  Register register_7 (.D(D7D6___________D0), .en(decoder_1_out6), .Q(register_7_q), .clk(clk));  // open: clr
  Register register_8 (.D(D7D6___________D0), .en(decoder_1_out7), .Q(register_8_q), .clk(clk));  // open: clr
  Register register_9 (.D(D7D6___________D0), .en(decoder_1_out8), .Q(register_9_q), .clk(clk));  // open: clr
  Register register_10 (.D(D7D6___________D0), .en(decoder_1_out9), .Q(register_10_q), .clk(clk));  // open: clr
  Register register_11 (.D(D7D6___________D0), .en(decoder_1_out10), .Q(register_11_q), .clk(clk));  // open: clr
  Register register_12 (.D(D7D6___________D0), .en(decoder_1_out11), .Q(register_12_q), .clk(clk));  // open: clr
  Register register_13 (.D(D7D6___________D0), .en(decoder_1_out12), .Q(register_13_q), .clk(clk));  // open: clr
  Register register_14 (.D(D7D6___________D0), .en(decoder_1_out13), .Q(register_14_q), .clk(clk));  // open: clr
  Register register_15 (.D(D7D6___________D0), .en(decoder_1_out14), .Q(register_15_q), .clk(clk));  // open: clr
  Register register_16 (.D(D7D6___________D0), .en(decoder_1_out15), .Q(register_16_q), .clk(clk));  // open: clr
  Hex_Digit_Display hex_digit_display_3 (.value(out_5[7:4]));  // open: dp
  Multiplexer #(.select(4), .width(8)) multiplexer_1 (
    .in0(register_1_q), .in1(register_2_q), .in2(register_3_q), .in3(register_4_q), .in4(register_5_q),
    .in5(register_6_q), .in6(register_7_q), .in7(register_8_q), .in8(register_9_q), .in9(register_10_q),
    .in10(register_11_q), .in11(register_12_q), .in12(register_13_q), .in13(register_14_q),
    .in14(register_15_q), .in15(register_16_q), .out(out_5), .sel(S3S2S1S0), .en(R_W_prime));
  Hex_Digit_Display hex_digit_display_4 (.value(out_5[3:0]));  // open: dp
endmodule

module Psw (
  input  [15:0] INPUT,
  input  [7:0] OP_2,
  input  [7:0] OP_1,
  output ODD_PARITY,
  output EVEN_PARITY,
  output ZERO,
  output SIGN_BIT,
  output HALF_CARRY
);

  Comparator #(.width(16)) comparator_1 (.a(INPUT), .b({16{1'b0}}), .eq(ZERO));  // open: gt, lt
  Adder #(.width(4)) adder_1 (.a(OP_2[3:0]), .b(OP_1[3:0]), .cout(HALF_CARRY));  // open: out, cin
  xor odd_parity_1 (ODD_PARITY, INPUT[0], INPUT[1], INPUT[2], INPUT[3], INPUT[4], INPUT[5], INPUT[6], INPUT[7], INPUT[9], INPUT[10], INPUT[11], INPUT[12], INPUT[13], INPUT[14], INPUT[15], INPUT[8]);
  xnor even_parity_1 (EVEN_PARITY, INPUT[0], INPUT[1], INPUT[2], INPUT[3], INPUT[4], INPUT[5], INPUT[6], INPUT[7], INPUT[9], INPUT[10], INPUT[11], INPUT[12], INPUT[13], INPUT[14], INPUT[15], INPUT[8]);

  assign SIGN_BIT = INPUT[8];

  // Notes on the sheet:
  //   ZERO
endmodule
